// Digital circuit 4-Bit-Adder.dig as structural Verilog
module _4_Bit_Adder (
  input  [3:0] A,
  input  [3:0] B,
  output [3:0] Output,
  output Overflow
);

  wire _1_bit_adder_1_p3, _1_bit_adder_2_p3, _1_bit_adder_3_p3;

  // _1_bit_adder _1_bit_adder_1: pin names not known; wires that end beside it: A[3], B[3], _1_bit_adder_1_p3, Output[3], Overflow
  // _1_bit_adder _1_bit_adder_2: pin names not known; wires that end beside it: A[2], B[2], _1_bit_adder_2_p3, Output[2], _1_bit_adder_1_p3
  // _1_bit_adder _1_bit_adder_3: pin names not known; wires that end beside it: A[1], B[1], _1_bit_adder_3_p3, Output[1], _1_bit_adder_2_p3
  // _1_bit_adder _1_bit_adder_4: pin names not known; wires that end beside it: A[0], B[0], 1'b0, Output[0], _1_bit_adder_3_p3
endmodule
