// Digital circuit 4-bit processor.dig as structural Verilog
module _4_bit_processor (
  input  [1:0] IR_Ctrl,
  input  [1:0] Memory_Ctrl,
  input  [3:0] Memory_Input,
  input  [1:0] PC_Ctrl,
  input  Sim_Clk,
  output [1:0] PC_Output,
  output [15:0] Instruction_Out,
  output [3:0] Read_Out_1,
  output [3:0] Read_Out_2,
  output [3:0] ALU_Out
);

  wire ir_memory_module_1_alu_enable;
  wire [7:0] multiplexer_1_out, registerfile_write_ctrl_1_write_out;

  IR_Memory_Module ir_memory_module_1 (
    .PC_Ctrl(PC_Ctrl), .clock(Sim_Clk), .IR_Memory_Input(Memory_Input), .IR_Memory_Ctrl(Memory_Ctrl),
    .IR_Ctrl(IR_Ctrl), .pc_output(PC_Output), .IR_Output(Instruction_Out),
    .ALU_enable(ir_memory_module_1_alu_enable));
  RegisterFile_Write_ctrl registerfile_write_ctrl_1 (
    .OpCode3(Instruction_Out[1:0]), .write_out(registerfile_write_ctrl_1_write_out));
  Multiplexer #(.Bits(8)) multiplexer_1 (
    .sel(ir_memory_module_1_alu_enable), .in_0({8{1'b0}}), .in_1(registerfile_write_ctrl_1_write_out),
    .out(multiplexer_1_out));
  Register_file_4_bit register_file_4_bit_1 (
    .Select_read1(Instruction_Out[5:4]), .Select_read2(Instruction_Out[3:2]), .clk(Sim_Clk),
    .Write_data(ALU_Out), .Select_write(Instruction_Out[1:0]), .ctrl_regs(multiplexer_1_out),
    .Read_data_1(Read_Out_1), .Read_Data_2(Read_Out_2));
  _4_bit_ALU _4_bit_alu_1 (
    .A(Read_Out_1), .B(Read_Out_2), .S1_S0_C_in(Instruction_Out[8:6]), .Output(ALU_Out));  // open: Overflow

  // Notes on the sheet:
  //   PC_Ctrl: default 1
endmodule

/* Test case Circuit Testing:
Sim-Clk IR-Ctrl Memory-Ctrl Memory-Input PC-Ctrl PC-Output Instruction-Out Read-Out-1 Read-Out-2 ALU-Out
c 0 1 0x0 1 x x x x x 
c 0 1 0x4 1 x x x x x 
c 0 1 0x1 1 x x x x x 
c 0 1 0x0 1 x x x x x 

c 0 1 0x0 1 x x x x x 
c 0 1 0x4 1 x x x x x 
c 0 1 0x1 1 x x x x x 
c 0 1 0x0 1 x x x x x 

c 0 1 0x5 1 x x x x x 
c 0 1 0x5 1 x x x x x 
c 0 1 0x1 1 x x x x x 
c 0 1 0x0 1 x x x x x 

c 0 1 0x6 1 x x x x x 
c 0 1 0x0 1 x x x x x 
c 0 1 0x0 1 x x x x x 
c 0 1 0x0 1 x x x x x

c 1 0 0x0 1 x x x x x 
c 1 0 0x4 1 x x x x x 
c 1 0 0x1 1 x x x x x 
c 1 0 0x0 1 x x x x x 

c 1 0 0x0 1 x x x x x 
c 1 0 0x4 1 x x x x x 
c 1 0 0x1 1 x x x x x 
c 1 0 0x0 1 x x x x x 

c 1 0 0x5 1 x x x x x 
c 1 0 0x5 1 x x x x x 
c 1 0 0x1 1 x x x x x 
c 1 0 0x0 1 x x x x x 

c 1 0 0x6 1 x x x x x 
c 1 0 0x0 1 x x x x x 
c 1 0 0x0 1 x x x x x 
c 1 0 0x0 1 x x x x x
*/
