// Digital circuit IR_Memory_Module.dig as structural Verilog
module IR_Memory_Module (
  input  [1:0] PC_Ctrl,
  input  clock,
  input  [3:0] IR_Memory_Input,
  input  [1:0] IR_Memory_Ctrl,
  input  [1:0] IR_Ctrl,
  output [1:0] pc_output,
  output [15:0] IR_Output,
  output ALU_enable
);

  wire not_1_out, not_2_out;
  wire [1:0] demultiplexer_1_out_0, demultiplexer_1_out_1, demultiplexer_1_out_2, demultiplexer_1_out_3;
  wire [3:0] _4_bit_instruction_register_1_output, _4_bit_instruction_register_2_output,
       _4_bit_instruction_register_3_output, _4_bit_instruction_register_4_output,
       _4x16_memory_dram_1_output, demultiplexer_2_out_0, demultiplexer_2_out_1, demultiplexer_2_out_2,
       demultiplexer_2_out_3;
  wire [3:2] program_counter_4_bit_1_output;

  Program_Counter_4_Bit program_counter_4_bit_1 (
    .CLK(clock), .Control(PC_Ctrl), .Output({program_counter_4_bit_1_output, pc_output}));
  _4x16_Memory_DRAM _4x16_memory_dram_1 (
    .Address({program_counter_4_bit_1_output, pc_output}), .Clock(clock), .Input(IR_Memory_Input),
    .Control(IR_Memory_Ctrl), .Output(_4x16_memory_dram_1_output));
  Demultiplexer #(.Selector_Bits(2), .Bits(2)) demultiplexer_1 (
    .sel(pc_output), .in(IR_Ctrl), .out_0(demultiplexer_1_out_0), .out_1(demultiplexer_1_out_1),
    .out_2(demultiplexer_1_out_2), .out_3(demultiplexer_1_out_3));
  Demultiplexer #(.Selector_Bits(2), .Bits(4)) demultiplexer_2 (
    .sel(pc_output), .in(_4x16_memory_dram_1_output), .out_0(demultiplexer_2_out_0),
    .out_1(demultiplexer_2_out_1), .out_2(demultiplexer_2_out_2), .out_3(demultiplexer_2_out_3));
  _4_Bit_Instruction_Register _4_bit_instruction_register_1 (
    .Clock(clock), .Control(demultiplexer_1_out_0), .Input(demultiplexer_2_out_0),
    .Output(_4_bit_instruction_register_1_output));
  _4_Bit_Instruction_Register _4_bit_instruction_register_2 (
    .Clock(clock), .Control(demultiplexer_1_out_1), .Input(demultiplexer_2_out_1),
    .Output(_4_bit_instruction_register_2_output));
  _4_Bit_Instruction_Register _4_bit_instruction_register_3 (
    .Clock(clock), .Control(demultiplexer_1_out_2), .Input(demultiplexer_2_out_2),
    .Output(_4_bit_instruction_register_3_output));
  _4_Bit_Instruction_Register _4_bit_instruction_register_4 (
    .Clock(clock), .Control(demultiplexer_1_out_3), .Input(demultiplexer_2_out_3),
    .Output(_4_bit_instruction_register_4_output));
  and and_1 (ALU_enable, not_1_out, not_2_out);
  not not_1 (not_1_out, pc_output[0]);
  not not_2 (not_2_out, pc_output[1]);
  assign IR_Output = ALU_enable ? {_4_bit_instruction_register_4_output, _4_bit_instruction_register_3_output, _4_bit_instruction_register_2_output, _4_bit_instruction_register_1_output} : 16'bz;  // Driver driver_1

  // Notes on the sheet:
  //   PC_Ctrl: default 1
endmodule
