// Digital circuit PC_Memory.dig as structural Verilog
module PC_Memory (
  input  Clk,
  input  [1:0] PC_Control,
  input  [3:0] Memory_Input,
  input  [1:0] Memory_Control,
  input  [3:0] User_Address,
  output [3:0] Output,
  output [3:0] PC_Out
);

  wire [3:0] or_1_out;

  Program_Counter_4_Bit program_counter_4_bit_1 (.CLK(Clk), .Control(PC_Control), .Output(PC_Out));
  assign or_1_out = User_Address | PC_Out;  // Or or_1, 4 bits wide
  _4x16_Memory_DRAM _4x16_memory_dram_1 (
    .Address(or_1_out), .Clock(Clk), .Input(Memory_Input), .Control(Memory_Control), .Output(Output));
endmodule
