// Digital circuit Program_Counter_4-Bit.dig as structural Verilog
module Program_Counter_4_Bit (
  input  CLK,
  input  [1:0] Control,
  output [3:0] Output
);

  wire [3:0] _4_bit_adder_1_output, multiplexer_1_out, not_1_out;

  _4_Bit_Adder _4_bit_adder_1 (.A(4'b0001), .B(Output), .Output(_4_bit_adder_1_output));  // open: Overflow
  assign not_1_out = ~4'b0000;  // Not not_1, 4 bits wide
  Multiplexer #(.Selector_Bits(2), .Bits(4)) multiplexer_1 (
    .sel(Control), .in_0(Output), .in_1(_4_bit_adder_1_output), .in_2(4'b0000), .in_3(not_1_out),
    .out(multiplexer_1_out));
  D_FF d_ff_1 (.D(multiplexer_1_out[3]), .C(CLK), .Q(Output[3]));  // open: nQ
  D_FF d_ff_2 (.D(multiplexer_1_out[2]), .C(CLK), .Q(Output[2]));  // open: nQ
  D_FF d_ff_3 (.D(multiplexer_1_out[1]), .C(CLK), .Q(Output[1]));  // open: nQ
  D_FF d_ff_4 (.D(multiplexer_1_out[0]), .C(CLK), .Q(Output[0]));  // open: nQ
endmodule
