// Digital circuit Register-file 4 bit.dig as structural Verilog
module Register_file_4_bit (
  input  [1:0] Select_read1,
  input  [1:0] Select_read2,
  input  clk,
  input  [3:0] Write_data,
  input  [1:0] Select_write,
  input  [7:0] ctrl_regs,
  output [3:0] Read_data_1,
  output [3:0] Read_Data_2
);

  wire [3:0] _4_bit_instruction_register_1_output, _4_bit_instruction_register_2_output,
       _4_bit_instruction_register_3_output, _4_bit_instruction_register_4_output, demultiplexer_1_out_0,
       demultiplexer_1_out_1, demultiplexer_1_out_2, demultiplexer_1_out_3;

  Demultiplexer #(.Selector_Bits(2), .Bits(4)) demultiplexer_1 (
    .sel(Select_write), .in(Write_data), .out_0(demultiplexer_1_out_0), .out_1(demultiplexer_1_out_1),
    .out_2(demultiplexer_1_out_2), .out_3(demultiplexer_1_out_3));
  _4_Bit_Instruction_Register _4_bit_instruction_register_1 (
    .Clock(clk), .Control(ctrl_regs[1:0]), .Input(demultiplexer_1_out_0),
    .Output(_4_bit_instruction_register_1_output));
  _4_Bit_Instruction_Register _4_bit_instruction_register_2 (
    .Clock(clk), .Control(ctrl_regs[3:2]), .Input(demultiplexer_1_out_1),
    .Output(_4_bit_instruction_register_2_output));
  _4_Bit_Instruction_Register _4_bit_instruction_register_3 (
    .Clock(clk), .Control(ctrl_regs[5:4]), .Input(demultiplexer_1_out_2),
    .Output(_4_bit_instruction_register_3_output));
  _4_Bit_Instruction_Register _4_bit_instruction_register_4 (
    .Clock(clk), .Control(ctrl_regs[7:6]), .Input(demultiplexer_1_out_3),
    .Output(_4_bit_instruction_register_4_output));
  Multiplexer #(.Selector_Bits(2), .Bits(4)) multiplexer_1 (
    .sel(Select_read1), .in_0(_4_bit_instruction_register_1_output),
    .in_1(_4_bit_instruction_register_2_output), .in_2(_4_bit_instruction_register_3_output),
    .in_3(_4_bit_instruction_register_4_output), .out(Read_data_1));
  Multiplexer #(.Selector_Bits(2), .Bits(4)) multiplexer_2 (
    .sel(Select_read2), .in_0(_4_bit_instruction_register_1_output),
    .in_1(_4_bit_instruction_register_2_output), .in_2(_4_bit_instruction_register_3_output),
    .in_3(_4_bit_instruction_register_4_output), .out(Read_Data_2));
endmodule
